# Fritzing sketch Esquemático y diseño Humedad (saved by Fritzing 0.9.3b)
circuit board: 8.46667cm x 5.64444cm
breadboards: 1

parts:
  SparkFun_ESP8266 = SparkFun ESP8266 Thing
  Chirp!_Soil_Moisture_Sensor1 = Chirp! Soil Moisture Sensor v2.7.3
  Componente2 = Adafruit ADS1115 16Bit I2C ADC [part_number="Adafruit #1085"]

nets:
  GND: SparkFun_ESP8266.GND, Chirp!_Soil_Moisture_Sensor1.pin_5, Componente2.ADDR, Componente2.GND
  VCC: SparkFun_ESP8266.VCC, Chirp!_Soil_Moisture_Sensor1.Pin_1, Componente2.VDD
  N1: SparkFun_ESP8266.GPIO2, Componente2.SDA
  N2: SparkFun_ESP8266.GPIO14, Componente2.SCL
  N3: SparkFun_ESP8266.RESET, SparkFun_ESP8266.GPIO16
  N4: Chirp!_Soil_Moisture_Sensor1.pin_3, Componente2.AIN0

custom parts:
  Adafruit ADS1115 16Bit I2C ADC: For microcontrollers without an analog-to-digital converter or when you want a higher-precision ADC, the ADS1115 provides 16-bit precision at 860 samples/second over I2C. The chip can be configured as 4 single-ended input channels, or two differential channels. As a nice bonus, it even includes a programmable gain amplifier, up to x16, to help boost up smaller single/differential signals to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
