# Fritzing sketch Esquemático y diseño Salinidad (saved by Fritzing 0.9.3b)
breadboards: 1

parts:
  ESP8266 = SparkFun ESP8266 Thing
  Componente2 = Adafruit ADS1115 16Bit I2C ADC [part_number="Adafruit #1085"]
  R1 = Resistor [tolerance=±5% resistance=10k package=THT]

nets:
  GND: ESP8266.GND, Componente2.ADDR, Componente2.GND, R1.Pin_1
  N1: ESP8266.GPIO2, Componente2.SDA
  N2: ESP8266.GPIO14, Componente2.SCL
  N3: ESP8266.RESET, ESP8266.GPIO16
  N4: ESP8266.USBVCC, Componente2.VDD
  N5: Componente2.AIN1, R1.Pin_0

custom parts:
  Adafruit ADS1115 16Bit I2C ADC: For microcontrollers without an analog-to-digital converter or when you want a higher-precision ADC, the ADS1115 provides 16-bit precision at 860 samples/second over I2C. The chip can be configured as 4 single-ended input channels, or two differential channels. As a nice bonus, it even includes a programmable gain amplifier, up to x16, to help boost up smaller single/differential signals to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
