# Fritzing sketch Esquemático y diseño VAAD_V1.1 (saved by Fritzing 0.9.3b)
breadboards: 1

parts:
  Chirp!_Soil_Moisture_Sensor2 = Chirp! Soil Moisture Sensor v2.7.3
  Componente3 = Adafruit ADS1115 16Bit I2C ADC [part_number="Adafruit #1085"]
  SparkFun_ESP8267 = SparkFun ESP8266 Thing
  R2 = Resistor [tolerance=±5% resistance=10k package=THT]

nets:
  VDD: Chirp!_Soil_Moisture_Sensor2.Pin_1, Componente3.VDD, SparkFun_ESP8267.VCC, SparkFun_ESP8267.USBVCC
  N1: Chirp!_Soil_Moisture_Sensor2.pin_3, Componente3.AIN0
  GND: Chirp!_Soil_Moisture_Sensor2.pin_5, Componente3.ADDR, Componente3.GND, SparkFun_ESP8267.GND, R2.Pin_1
  N2: Componente3.AIN1, R2.Pin_0
  N3: Componente3.SDA, SparkFun_ESP8267.GPIO2
  N4: Componente3.SCL, SparkFun_ESP8267.GPIO14
  N5: SparkFun_ESP8267.RESET, SparkFun_ESP8267.GPIO16

custom parts:
  Adafruit ADS1115 16Bit I2C ADC: For microcontrollers without an analog-to-digital converter or when you want a higher-precision ADC, the ADS1115 provides 16-bit precision at 860 samples/second over I2C. The chip can be configured as 4 single-ended input channels, or two differential channels. As a nice bonus, it even includes a programmable gain amplifier, up to x16, to help boost up smaller single/differential signals to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
