# Fritzing sketch Esquemático y Diseño Temperatura (saved by Fritzing 0.9.3b)
breadboards: 1

parts:
  Componente1 = SparkFun ESP8266 Thing
  Componente2 = ADS1115
  R1 = Temperature Sensor (Thermistor) [thermistor_type=NTC package=THT]
  R2 = Resistor [tolerance=±5% resistance=2.2k package=THT]

nets:
  GND: Componente1.GND, Componente2.GND, Componente2.ADDR, R2.Pin_0
  N1: Componente1.VCC, R1.pin_0
  N2: Componente1.GPIO2, Componente2.SDA
  N3: Componente1.GPIO14, Componente2.SCL
  N4: Componente1.RESET, Componente1.GPIO16
  N5: Componente1.USBVCC, Componente2.VDD
  N6: Componente2.A2, R1.pin_1, R2.Pin_1

custom parts:
  ADS1115: ADC ADS1115
